// Logisim project CRC.circ as structural Verilog: 1 circuit, main circuit main
module main (
  input  Input__switch,
  input  Clock__Serial,
  input  Vcc,
  output MSB,
  output out_5,
  output out_6,
  output LSB
);

  wire not_1_out, not_2_out, not_3_out, not_4_out, xor_1_out, xor_2_out;

  xor xor_1 (xor_1_out, MSB, Input__switch);
  J_K_Flip_Flop #(.trigger("falling")) j_k_ff_1 (
    .J(xor_1_out), .clk(Clock__Serial), .K(not_1_out), .Q(LSB), .preset(1'b0), .en(1'b1), .reset(Vcc));  // open: Qn
  not not_1 (not_1_out, xor_1_out);
  not not_2 (not_2_out, LSB);
  J_K_Flip_Flop #(.trigger("falling")) j_k_ff_2 (
    .J(LSB), .clk(Clock__Serial), .K(not_2_out), .Q(out_6), .preset(1'b0), .en(1'b1), .reset(Vcc));  // open: Qn
  not not_3 (not_3_out, out_6);
  J_K_Flip_Flop #(.trigger("falling")) j_k_ff_3 (
    .J(out_6), .clk(Clock__Serial), .K(not_3_out), .Q(out_5), .preset(1'b0), .en(1'b1), .reset(Vcc));  // open: Qn
  xor xor_2 (xor_2_out, MSB, out_5);
  not not_4 (not_4_out, xor_2_out);
  J_K_Flip_Flop #(.trigger("falling")) j_k_ff_4 (
    .J(xor_2_out), .clk(Clock__Serial), .K(not_4_out), .Q(MSB), .preset(1'b0), .en(1'b1), .reset(Vcc));  // open: Qn

  // Notes on the sheet:
  //   CLEAR (switch)
  //   REMAINDER =>
  //   G(x) = x^4 + x^3 + 1 = 1 1 0 0 1
  //   LSB
  //   MSB
endmodule
